# Fritzing sketch cooler (saved by Fritzing 0.9.3b)
perfboards: 1

parts:
  External_Pullup = Resistor [tolerance=±5% resistance=4.7k package="0603 [SMD]"]
  FAN = IC, DIP package, 4 pins [chip_label=IC]
  Traco_Power_Supply = SO08-EIAJ [chip_label=THD-12WI package=SO]
  Sensor_Jumper = Header 3 [package=molex-1x3_lock]
  Fan_Jumper = Header 2 [package=molex-1x2_lock]
  DS1 = DS18B20 1-Wire Temperature Sensor [part_number=DS18B20]
  U1 = ATMEGA32U4 [package=qfn]

nets:
  Pin 7: External_Pullup.Pin_0, Sensor_Jumper.2, DS1.DQ, U1.PD7(ADC10)
  5V: External_Pullup.Pin_1, Sensor_Jumper.1, DS1.VDD, U1.VCC
  24V/Supply Voltage: FAN.pin1, Traco_Power_Supply.6
  Supply GND: FAN.pin2, Traco_Power_Supply.3, Sensor_Jumper.3, Fan_Jumper.2, DS1.GND, U1.GND
  Pin 9: FAN.pin4, Fan_Jumper.1, U1.PB5(ADC12)
  12V: Traco_Power_Supply.8, U1.VBUS
